# Fritzing sketch Master (saved by Fritzing 1.0.1rc)
breadboards: 2

parts:
  Part1 = Breadboard Power Supply Board SMD
  µC1 = ATmega32 [package=dip]
  Part2 = Bluetooth HM-11
  S1 = Pushbutton [package="[SMD]"]
  Q1 = NPN-Transistor [package="TO92 [THT]"]
  SP1 = SPEAKER [package=pcb_mount_speaker]
  LED1 = LED - 3mm [color="Red (633nm)" current=0.030 package="3 mm [THT]"]
  LED2 = LED - 3mm [color="Red (633nm)" current=0.030 package="3 mm [THT]"]
  R1 = Resistor [tolerance=±5% resistance=220 package="1206 [SMD]"]
  R2 = Resistor [tolerance=±5% resistance=220 package="1206 [SMD]"]
  OLED_I2C1 = OLED 128x64 I2C Monochrome Display
  R3 = Resistor [tolerance=±5% power=0.25 resistance=220 package=THT]
  R4 = Resistor [tolerance=±5% power=0.25 resistance=220 package=THT]
  Part3 = Adafruit Analog 2-Axis Joystick [part_number="Adafruit #512"]

nets:
  GND: Part1.GND, µC1.GND1, µC1.GND2, Part2.GND, S1.Pin_1, S1.Pin_2, SP1.+, R1.Pin_1, R2.Pin_1, OLED_I2C1.GND, R3.Pin_1, Part3.GND
  VCC: Part1.VCC, µC1.VCC, µC1.AVCC, Q1.E, OLED_I2C1.VDD, R4.Pin_0, Part3.VCC
  N1: µC1.PB0, Q1.B
  N2: µC1.RESET, S1.Pin_3, S1.Pin_4
  N3: µC1.PD0, Part2.UART_TX
  N4: µC1.PD1, Part2.UART_RX
  N5: µC1.PD2, Part3.SWITCH
  N6: µC1.PD5, LED1.cathode
  N7: µC1.PD7, LED2.cathode
  N8: µC1.PC0, OLED_I2C1.SCK
  N9: µC1.PC1, OLED_I2C1.SDA
  N10: µC1.AREF, R3.Pin_0, R4.Pin_1
  N11: µC1.PA2, Part3.YOUT
  N12: µC1.PA1, Part3.XOUT
  N13: Part2.VCC, Q1.C
  N14: LED1.anode, R2.Pin_0
  N15: LED2.anode, R1.Pin_0

custom parts:
  ATmega32: AVR 8-bit microcontroller.
  Adafruit Analog 2-Axis Joystick: This mini-kit makes it easy to mount a PSP/Xbox-like thumb joystick to your project. The thumbstick is an analog joystick - more accurate and sensitive than just 'directional' joysticks - with a 'press in to select' button. Since it's analog, you'll need two analog reading pins on your microcontroller to determine X and Y. Having an extra digital input will let you read the switch. The pack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
