# Fritzing sketch Slave (saved by Fritzing 1.0.1rc)
breadboards: 1

parts:
  µC1 = ATmega32 [package=dip]
  Part1 = Bluetooth HM-11
  Part2 = Breadboard Power Supply Board SMD
  HC-SR04_Sensor_2 = HC-SR04 Ultrasonic Distance Sensor

nets:
  VCC: µC1.VCC, Part1.VCC, Part2.VCC, HC-SR04_Sensor_2.VCC
  GND: µC1.GND1, µC1.GND2, Part1.GND, Part2.GND, HC-SR04_Sensor_2.GND
  N1: µC1.PD0, Part1.UART_TX
  N2: µC1.PD1, Part1.UART_RX
  N3: µC1.PC0, HC-SR04_Sensor_2.TRIG_RX_SCL_I/O
  N4: µC1.PC1, HC-SR04_Sensor_2.ECHO_TX_SDA

custom parts:
  ATmega32: AVR 8-bit microcontroller.
  HC-SR04 Ultrasonic Distance Sensor: The HC-SR04 is an ultrasonic distance sensor. It is capable of providing measurement for ranges of 2cm to 400cm. The module operates at 5V.
