# Fritzing sketch Untitled Sketch 2 (saved by Fritzing 1.0.1rc)
breadboards: 1

parts:
  µC1 = ATmega32 [package=dip]
  HC-SR04_Sensor_1 = HC-SR04 Ultrasonic Distance Sensor
  Part1 = Bluetooth HM-11
  Part2 = Breadboard Power Supply Board SMD

nets:
  GND1: µC1.GND1, µC1.GND2
  N1: µC1.PD0, Part1.UART_TX
  N2: µC1.PD1, Part1.UART_RX
  N3: µC1.PC0, HC-SR04_Sensor_1.TRIG
  N4: µC1.PC1, HC-SR04_Sensor_1.ECHO
  VCC: Part1.VCC, Part2.VCC
  GND: Part1.GND, Part2.GND

custom parts:
  ATmega32: AVR 8-bit microcontroller.
